// Logisim project WITCPU.circ as structural Verilog: 5 circuits, main circuit RegisterR10
module main (
  input  [15:0] data,
  input  tick,
  input  [1:0] rx,
  input  [1:0] ry,
  input  [3:0] Rd,
  output [15:0] out_6,
  output [15:0] out_7
);

  wire demultiplexer_1_out0, demultiplexer_1_out1, demultiplexer_1_out2, demultiplexer_1_out3;
  wire [15:0] group_1_out_6, group_1_out_7, group_2_out_6, group_2_out_7, group_3_out_6, group_3_out_7,
       registerr10_1_out_6, registerr10_1_out_7;

  Demultiplexer #(.select(2)) demultiplexer_1 (
    .out0(demultiplexer_1_out0), .out1(demultiplexer_1_out1), .out2(demultiplexer_1_out2),
    .out3(demultiplexer_1_out3), .in(tick), .sel(Rd[1:0]));  // open: en
  RegisterR10 registerr10_1 (
    .in_1(data), .tick(demultiplexer_1_out0), .Ra(ry), .in_4(Rd[3:2]), .in_5(rx),
    .out_6(registerr10_1_out_6), .out_7(registerr10_1_out_7));
  group group_1 (
    .in_1(data), .tick(demultiplexer_1_out1), .in_3(ry), .in_4(Rd[3:2]), .in_5(rx), .out_6(group_1_out_6),
    .out_7(group_1_out_7));
  group group_2 (
    .in_1(data), .tick(demultiplexer_1_out2), .in_3(ry), .in_4(Rd[3:2]), .in_5(rx), .out_6(group_2_out_6),
    .out_7(group_2_out_7));
  group group_3 (
    .in_1(data), .tick(demultiplexer_1_out3), .in_3(ry), .in_4(Rd[3:2]), .in_5(rx), .out_6(group_3_out_6),
    .out_7(group_3_out_7));
  Multiplexer #(.select(2), .width(16)) multiplexer_1 (
    .in0(registerr10_1_out_6), .in1(group_1_out_6), .in2(group_2_out_7), .in3(group_3_out_6), .out(out_6),
    .sel(Rd[1:0]));  // open: en
  Multiplexer #(.select(2), .width(16)) multiplexer_2 (
    .in0(registerr10_1_out_7), .in1(group_1_out_7), .in2(group_2_out_6), .in3(group_3_out_7), .out(out_7),
    .sel(Rd[1:0]));  // open: en
endmodule

module RegisterR10 (
  input  [15:0] in_1,
  input  tick,
  input  [1:0] Ra,
  input  [1:0] in_4,
  input  [1:0] in_5,
  output [15:0] out_6,
  output [15:0] out_7
);

  wire demultiplexer_1_out0, demultiplexer_1_out1, demultiplexer_1_out2, demultiplexer_1_out3;
  wire [15:0] register_1_q, register_2_q, register_3_q, register_4_q;

  Demultiplexer #(.select(2)) demultiplexer_1 (
    .out0(demultiplexer_1_out0), .out1(demultiplexer_1_out1), .out2(demultiplexer_1_out2),
    .out3(demultiplexer_1_out3), .in(tick), .sel(in_4));  // open: en
  ALU alu_1 ();  // open: Enable, opcode, x, y, imm, out_6
  Register #(.width(16)) register_1 (.D({16{1'b0}}), .Q(register_1_q), .clk(demultiplexer_1_out0));  // open: en, clr
  Register #(.width(16)) register_2 (.D(in_1), .Q(register_2_q), .clk(demultiplexer_1_out1));  // open: en, clr
  Register #(.width(16)) register_3 (.D(in_1), .Q(register_3_q), .clk(demultiplexer_1_out2));  // open: en, clr
  Register #(.width(16)) register_4 (.D(in_1), .Q(register_4_q), .clk(demultiplexer_1_out3));  // open: en, clr
  Multiplexer #(.select(2), .width(16)) multiplexer_1 (
    .in0(register_1_q), .in1(register_2_q), .in2(register_3_q), .in3(register_4_q), .out(out_6), .sel(Ra));  // open: en
  Multiplexer #(.select(2), .width(16)) multiplexer_2 (
    .in0(register_1_q), .in1(register_2_q), .in2(register_3_q), .in3(register_4_q), .out(out_7), .sel(in_5));  // open: en
endmodule

module group (
  input  [15:0] in_1,
  input  tick,
  input  [1:0] in_3,
  input  [1:0] in_4,
  input  [1:0] in_5,
  output [15:0] out_6,
  output [15:0] out_7
);

  wire demultiplexer_1_out0, demultiplexer_1_out1, demultiplexer_1_out2, demultiplexer_1_out3;
  wire [15:0] register_1_q, register_2_q, register_3_q, register_4_q;

  Demultiplexer #(.select(2)) demultiplexer_1 (
    .out0(demultiplexer_1_out0), .out1(demultiplexer_1_out1), .out2(demultiplexer_1_out2),
    .out3(demultiplexer_1_out3), .in(tick), .sel(in_4));  // open: en
  Register #(.width(16)) register_1 (.D(in_1), .Q(register_1_q), .clk(demultiplexer_1_out0));  // open: en, clr
  Register #(.width(16)) register_2 (.D(in_1), .Q(register_2_q), .clk(demultiplexer_1_out1));  // open: en, clr
  Register #(.width(16)) register_3 (.D(in_1), .Q(register_3_q), .clk(demultiplexer_1_out2));  // open: en, clr
  Register #(.width(16)) register_4 (.D(in_1), .Q(register_4_q), .clk(demultiplexer_1_out3));  // open: en, clr
  Multiplexer #(.select(2), .width(16)) multiplexer_1 (
    .in0(register_1_q), .in1(register_2_q), .in2(register_3_q), .in3(register_4_q), .out(out_6), .sel(in_3));  // open: en
  Multiplexer #(.select(2), .width(16)) multiplexer_2 (
    .in0(register_1_q), .in1(register_2_q), .in2(register_3_q), .in3(register_4_q), .out(out_7), .sel(in_5));  // open: en
endmodule

module ALU (
  input  Enable,
  input  [3:0] opcode,
  input  [15:0] x,
  input  [15:0] y,
  input  [7:0] imm,
  output [15:0] out_6
);

  wire [15:0] adder_1_out, and_1_out, divider_1_out, multiplier_1_out, or_1_out, subtractor_1_out, xnor_1_out;

  Adder #(.width(16)) adder_1 (.a(x), .b(y), .out(adder_1_out));  // open: cin, cout
  Subtractor #(.width(16)) subtractor_1 (.a(x), .b(y), .out(subtractor_1_out));  // open: bin, bout
  Multiplier #(.width(16)) multiplier_1 (.a(x), .b(y), .out(multiplier_1_out));  // open: cin, cout
  Divider #(.width(16)) divider_1 (.a(x), .b(y), .out(divider_1_out));  // open: upper, rem
  assign and_1_out = x & y;  // AND_Gate and_1, 16 bits wide
  assign or_1_out = x | y;  // OR_Gate or_1, 16 bits wide
  assign xnor_1_out = ~(x ^ y);  // XNOR_Gate xnor_1, 16 bits wide
  Multiplexer #(.select(4), .width(16)) multiplexer_1 (
    .in0(adder_1_out), .in1(subtractor_1_out), .in2(multiplier_1_out), .in3(divider_1_out), .in4(and_1_out),
    .in5(or_1_out), .in6(xnor_1_out), .in7({{8{1'b0}}, imm}), .out(out_6), .sel(opcode), .en(Enable));  // open: in8, in9, in10, in11, in12, in13, in14, in15
endmodule

module Decoder (
  input  [15:0] \input ,
  output [3:0] opcode,
  output [3:0] Rd,
  output [3:0] operand1,
  output [3:0] operand2,
  output [7:0] out_6
);

  Multiplexer #(.width(4)) multiplexer_1 (
    .in0(\input [3:0]), .in1(\input [7:4]), .out(operand2), .sel(\input [15]));  // open: en

  assign opcode = \input [15:12];
  assign operand1 = \input [7:4];
  assign out_6 = \input [7:0];
  assign Rd = \input [11:8];
endmodule
